// Digital circuit alu.dig as structural Verilog
module alu (
  input  [15:0] D_1,
  input  [15:0] D_2,
  input  [15:0] ADD_instr,
  input  [15:0] ADDR_instr,
  input  [15:0] SUB_instr,
  input  [15:0] SUBR_instr,
  input  [15:0] MUL_instr,
  input  [15:0] MULR_instr,
  output [1:0] rs_1,
  output [15:0] D_res,
  output [1:0] rd,
  output en,
  output [1:0] rs_2,
  output ovf
);

  wire [23:0] adder_1_add_merged, multiplier_1_mul_merged, subtractor_1_sub_merged;

  adder adder_1 (.ADD_instr(ADD_instr), .ADDR_instr(ADDR_instr), .D_1(D_1), .D_2(D_2), .add_merged(adder_1_add_merged));
  subtractor subtractor_1 (
    .SUB_instr(SUB_instr), .SUBR_instr(SUBR_instr), .D_1(D_1), .D_2(D_2), .sub_merged(subtractor_1_sub_merged));
  multiplier multiplier_1 (
    .MUL_instr(MUL_instr), .MULR_instr(MULR_instr), .D_1(D_1), .D_2(D_2), .mul_merged(multiplier_1_mul_merged));
  assign {ovf, D_res, rs_2, rs_1, rd, en} = adder_1_add_merged | subtractor_1_sub_merged | multiplier_1_mul_merged;  // Or or_1, 24 bits wide
endmodule
