// Digital circuit cache.dig as structural Verilog
module cache (
  input  [15:0] LD_instr,
  input  [15:0] RAM_i,
  input  C,
  input  [15:0] ST_instr,
  input  [1:0] rs_1,
  input  [15:0] D_in,
  input  [1:0] rd,
  input  en,
  input  [1:0] rs_2,
  input  [1:0] rs_3,
  output [5:0] addr,
  output ld,
  output st,
  output [15:0] RAM_o,
  output [15:0] D_o1,
  output [15:0] D_o2,
  output [15:0] D_o3
);

  wire decoder_1_out_0, or_1_out;
  wire [1:0] priorityencoder_1_num, rd_t, rs_1_t, rs_store;
  wire [4:0] demultiplexer_2_out_0;
  wire [4:2] demultiplexer_2_out_1;
  wire [5:0] ld_addr;
  wire [8:0] demultiplexer_1_out_0;
  wire [8:6] demultiplexer_1_out_1;
  wire [15:0] D_ld, D_reg;

  Multiplexer #(.Bits(2)) multiplexer_1 (.sel(ST_instr[1]), .in_0(rs_1), .in_1(rs_store), .out(rs_1_t));
  // Probe on LD_instr[3:1]
  Decoder decoder_1 (.sel(LD_instr[6]), .out_0(decoder_1_out_0), .out_1(ld));
  // Probe on decoder_1_out_0
  Demultiplexer #(.Bits(9)) demultiplexer_1 (
    .sel(LD_instr[6]), .in(LD_instr[15:7]), .out_0(demultiplexer_1_out_0),
    .out_1({demultiplexer_1_out_1, ld_addr}));
  Demultiplexer #(.Bits(5)) demultiplexer_2 (
    .sel(ST_instr[10]), .in(ST_instr[15:11]), .out_0(demultiplexer_2_out_0),
    .out_1({demultiplexer_2_out_1, rs_store}));
  PriorityEncoder #(.Selector_Bits(2)) priorityencoder_1 (
    .in0(1'b1), .in1(ld), .in2(ST_instr[1]), .in3(1'b0), .num(priorityencoder_1_num));  // open: any
  Multiplexer #(.Bits(16)) multiplexer_2 (.sel(LD_instr[0]), .in_0(D_in), .in_1(D_ld), .out(D_reg));
  Multiplexer #(.Bits(16)) multiplexer_3 (
    .sel(LD_instr[6]), .in_0({{7{1'b0}}, demultiplexer_1_out_0}), .in_1(RAM_i), .out(D_ld));
  Multiplexer #(.Bits(16)) multiplexer_4 (
    .sel(ST_instr[10]), .in_0({{11{1'b0}}, demultiplexer_2_out_0}), .in_1(D_o1), .out(RAM_o));
  Multiplexer #(.Selector_Bits(2), .Bits(6)) multiplexer_5 (
    .sel(priorityencoder_1_num), .in_0({6{1'b0}}), .in_1(ld_addr), .in_2(ST_instr[9:4]), .in_3({6{1'b0}}),
    .out(addr));
  Multiplexer #(.Bits(2)) multiplexer_6 (.sel(LD_instr[0]), .in_0(rd), .in_1(LD_instr[5:4]), .out(rd_t));
  or or_1 (or_1_out, en, LD_instr[0]);
  regfile regfile_1 (
    .en(or_1_out), .rd(rd_t), .D_i(D_reg), .C(C), .rs_1(rs_1_t), .rs_2(rs_2), .rs_3(rs_3), .D_o1(D_o1),
    .D_o2(D_o2), .D_o3(D_o3));

  assign st = ST_instr[1];

  // Other names for the same wires on the sheet: st_addr[5:0] = ST_instr[9:4]
endmodule
