// Digital circuit control.dig as structural Verilog
module control (
  input  [15:0] JMP_instr,
  output [15:0] instr,
  output [5:0] A_in,
  output en
);

  Comparator #(.Bits(4)) comparator_1 (.a(JMP_instr[3:0]), .b(4'b1010), .eq(en));  // open: gt, lt
  Multiplexer #(.Bits(6)) multiplexer_1 (.sel(en), .in_0({6{1'b0}}), .in_1(JMP_instr[9:4]), .out(A_in));
  Multiplexer #(.Bits(16)) multiplexer_2 (.sel(en), .in_0(JMP_instr), .in_1({16{1'b0}}), .out(instr));
endmodule
