// Digital circuit decoder.dig as structural Verilog
module decoder (
  input  [15:0] instr_i,
  output [15:0] NOP,
  output [15:0] HALT,
  output [15:0] LD,
  output [15:0] ST,
  output [15:0] ADD,
  output [15:0] ADDR,
  output [15:0] SUB,
  output [15:0] SUBR,
  output [15:0] MUL,
  output [15:0] MULR,
  output [15:0] JMP,
  output [15:0] JEQ,
  output [15:0] JLT,
  output [15:0] JGT,
  output [15:0] INC
);

  Demultiplexer #(.Selector_Bits(4), .Bits(16)) demultiplexer_1 (
    .sel(instr_i[3:0]), .in(instr_i), .out_0(NOP), .out_1(HALT), .out_2(LD), .out_3(ST), .out_4(ADD),
    .out_5(ADDR), .out_6(SUB), .out_7(SUBR), .out_8(MUL), .out_9(MULR), .out_10(JMP), .out_11(JEQ),
    .out_12(JLT), .out_13(JGT), .out_14(INC));  // open: out_15
  // Probe on instr_i[15:4]
endmodule
