// Digital circuit fetch.dig as structural Verilog
module fetch (
  input  C,
  output error,
  output halt,
  output [15:0] D_o,
  output [15:0] D_o2,
  output [15:0] D_o3,
  output gt,
  output eq,
  output lt,
  output [15:0] D_o4
);

  wire alu_1_en, C_t, control_1_en, decoder_1_out_0, decoder_2_p3, err, jmp, ld_en, load, move, st_en, store;
  wire [1:0] alu_1_rd, alu_1_rs_1, alu_1_rs_2, control_1_rs, priorityencoder_1_num;
  wire [5:0] _1A, control_1_a_new, counterpreset_1_out;
  wire [15:0] add, addr, alu_1_d_res, control_1_instr_o, D_in, halt_t, IR_q, mul, mulr, ramdualaccess_1_d1,
       ramdualaccess_1_d2, sub, subr;

  CounterPreset #(.maxValue(32), .Bits(6), .isProgramCounter("true")) counterpreset_1 (
    .en(1'b1), .C(C_t), .dir(1'b0), .in(control_1_a_new), .ld(control_1_en), .clr(1'b0),
    .out(counterpreset_1_out), .ovf(err));
  PriorityEncoder #(.Selector_Bits(2)) priorityencoder_1 (
    .in0(1'b1), .in1(halt_t[0]), .in2(err), .in3(1'b0), .num(priorityencoder_1_num));  // open: any
  Decoder #(.Selector_Bits(2)) decoder_1 (
    .sel(priorityencoder_1_num), .out_0(decoder_1_out_0), .out_1(halt), .out_2(error));  // open: out_3
  alu alu_1 (
    .D_1(D_o), .D_2(D_o2), .ADD_instr(add), .ADDR_instr(addr), .SUB_instr(sub), .SUBR_instr(subr),
    .MUL_instr(mul), .MULR_instr(mulr), .rs_1(alu_1_rs_1), .D_res(alu_1_d_res), .rd(alu_1_rd), .en(alu_1_en),
    .rs_2(alu_1_rs_2), .ovf(err));
  and and_1 (C_t, C, decoder_1_out_0);
  RAMDualAccess #(.AddrBits(6), .isProgramMemory("true"), .Bits(16)) ramdualaccess_1 (
    .str(st_en), .C(C_t), .ld(ld_en), .A1(_1A), .Din1(D_in), .A2(counterpreset_1_out),
    .D1(ramdualaccess_1_d1), .D2(ramdualaccess_1_d2));
  control control_1 (
    .instr_in(ramdualaccess_1_d2), .D_rs(D_o3), .C(C_t), .rs(control_1_rs), .instr_o(control_1_instr_o),
    .gt(gt), .eq(eq), .lt(lt), .A_new(control_1_a_new), .en(control_1_en));
  // cache cache_1: pin names not known; wires that end beside it: load, ramdualaccess_1_d1, C_t, store, alu_1_rs_1, alu_1_d_res, alu_1_rd, alu_1_en, alu_1_rs_2, move, control_1_rs, _1A, ld_en, st_en, D_in, D_o, D_o2, D_o3, D_o4
  Register #(.Bits(16)) IR (.D(control_1_instr_o), .C(C_t), .en(1'b1), .Q(IR_q));
  // decoder decoder_2: pin names not known; wires that end beside it: IR_q, C_t, decoder_2_p3, load, store, move, add, addr, sub, subr, mul, mulr, jmp, halt_t
  // Probe on decoder_2_p3

  // Notes on the sheet:
  //   C: Hz: 2
endmodule
