// Digital circuit regfile.dig as structural Verilog
module regfile (
  input  [1:0] rd,
  input  [15:0] D_i,
  input  clk,
  input  [1:0] rs,
  output [15:0] D_o
);

  wire decoder_1_out_0, decoder_1_out_1, decoder_1_out_2, decoder_1_out_3;
  wire [15:0] demultiplexer_1_out_0, demultiplexer_1_out_1, demultiplexer_1_out_2, demultiplexer_1_out_3,
       R0_q, R1_q, R2_q, R3_q;

  Demultiplexer #(.Selector_Bits(2), .Bits(16)) demultiplexer_1 (
    .sel(rd), .in(D_i), .out_0(demultiplexer_1_out_0), .out_1(demultiplexer_1_out_1),
    .out_2(demultiplexer_1_out_2), .out_3(demultiplexer_1_out_3));
  Decoder #(.Selector_Bits(2)) decoder_1 (
    .sel(rd), .out_0(decoder_1_out_0), .out_1(decoder_1_out_1), .out_2(decoder_1_out_2),
    .out_3(decoder_1_out_3));
  Register #(.Bits(16)) R0 (.D(demultiplexer_1_out_0), .C(clk), .en(decoder_1_out_0), .Q(R0_q));
  Register #(.Bits(16)) R1 (.D(demultiplexer_1_out_1), .C(clk), .en(decoder_1_out_1), .Q(R1_q));
  Register #(.Bits(16)) R2 (.D(demultiplexer_1_out_2), .C(clk), .en(decoder_1_out_2), .Q(R2_q));
  Register #(.Bits(16)) R3 (.D(demultiplexer_1_out_3), .C(clk), .en(decoder_1_out_3), .Q(R3_q));
  Multiplexer #(.Bits(16), .Selector_Bits(2)) multiplexer_1 (
    .sel(rs), .in_0(R0_q), .in_1(R1_q), .in_2(R2_q), .in_3(R3_q), .out(D_o));

  // Other names for the same wires on the sheet: C = clk
endmodule
